# Fritzing sketch Circuit (saved by Fritzing 0.9.3b)
circuit board: 8.46667cm x 5.64444cm
breadboards: 1

parts:
  A1 = ESP32 DOIT DEVKIT V1 36pin
  Part1 = SRF05 Ultrasonic Rangefinder
  OLED1 = OLED 128x64 I2C Monochrome Display GND-VDD
  SG1 = Buzzer 12mm [package=buzzer-cmt1102]

nets:
  N1: A1.Pin_17, Part1.GND
  N2: A1.Pin_18, Part1.VCC
  N3: A1.Pin_19, OLED1.VDD
  N4: A1.Pin_20, OLED1.GND, SG1.2
  N5: A1.Pin_29, Part1.Trig
  N6: A1.Pin_30, Part1.Echo
  N7: A1.Pin_31, SG1.1
  N8: A1.Pin_32, OLED1.SDA
  N9: A1.Pin_35, OLED1.SCK

custom parts:
  ESP32 DOIT DEVKIT V1 36pin: ESP32 DOIT DEVKIT V1 36pin.
  OLED 128x64 I2C Monochrome Display GND-VDD: OLED 128x64 I2C Monochrome Display. Note: there are two variants of this part, this one is the GND VDD SCK SDA variant. The other is VDD GND SCK SDA. Make sure you select the part that matches your module as using the incorrect part will probably destroy your module! In addition the mounting holes are marked on silkscreen but not by default drilled. If you want drilled mounting holes, copy a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
